# Fritzing sketch HubWiringDiagram (saved by Fritzing 0.9.3b)

parts:
  Part1 = adafruit [part_number="Adafruit #3078 and Adafruit #3079"]
  Part2 = adafruit [part_number="Adafruit #3201"]
  Part3 = Adafruit Adalogger FeatherWing [part_number="Adafruit #2922"]

nets:
  N1: Part1.connector64, Part2.connector82, Part3.G, Part3.TX
  N2: Part1.connector65, Part2.connector81, Part3.RX
  N3: Part1.connector66, Part2.connector80, Part3.MISO
  N4: Part1.connector67, Part2.connector79, Part3.MOSI
  N5: Part1.connector68, Part2.connector78, Part3.SCK
  N6: Part1.connector69, Part2.connector77, Part3.F
  N7: Part1.connector70, Part2.connector76, Part3.E
  N8: Part1.connector71, Part2.connector75, Part3.D
  N9: Part1.connector72, Part2.connector74, Part3.C
  N10: Part1.connector73, Part2.connector73, Part3.B
  N11: Part1.connector74, Part2.connector72, Part3.A
  N12: Part1.connector75, Part2.connector71, Part3.GND
  N13: Part1.connector76, Part2.connector70, Part3.AREF
  N14: Part1.connector77, Part2.connector69, Part3.+3V3
  N15: Part1.connector78, Part2.connector68, Part3.RESET
  N16: Part1.connector79, Part2.connector67
  N17: Part1.connector80, Part2.connector94
  N18: Part1.connector81, Part2.connector93, Part3.VBAT
  N19: Part1.connector82, Part2.connector92, Part3.EN
  N20: Part1.connector83, Part2.connector91, Part3.N, Part3.USB
  N21: Part1.connector85, Part2.connector89, Part3.M
  N22: Part1.connector86, Part2.connector88, Part3.L
  N23: Part1.connector87, Part2.connector87, Part3.CS
  N24: Part1.connector88, Part2.connector86, Part3.J
  N25: Part1.connector89, Part2.connector85, Part3.I
  N26: Part1.connector90, Part2.connector84, Part3.H
  N27: Part1.connector91, Part2.connector83, Part3.SDA, Part3.SCL

custom parts:
  Adafruit Adalogger FeatherWing: This is the Adalogger FeatherWing: it adds both a battery-backed Real Time Clock and micro SD card storage to any Feather main board. This FeatherWing will make it real easy to add datalogging to any of our existing Feathers. You get both an I2C real time clock (PCF8523) with 32KHz crystal and battery backup, and a microSD socket that connects to the SPI port pins (+ extra pin for CS). Tested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
